# Fritzing sketch automated_blinds (saved by Fritzing 1.0.6)

parts:
  Adafruit_TMC2209_Stepper_Motor_Driver1 = Adafruit TMC2209 Stepper Motor Driver [part_number=#6121]
  esp1 = ESP32 DevKitc V4
  12V_5-10A_DC = 2.1mm Barrel Jack with Terminal Block
  M3 = RioRand LM2596
  M2 = Stepper Motor - Bipolar
  R2 = Resistor [tolerance=±5% power=0.25W resistance=10000 package=THT]
  25V_100mf = Capacitor Polarized [package=nippon_f80]
  J1 = female pin header, 10 pins [form="♀ (female)"]
  J2 = female pin header, 3 pins [form="♀ (female)"]
  R1 = Photocell (LDR) [power=0.25W dark_resistance_@0.01lx=300kΩ light_resistance_@100lx=400Ω luminance=10lx package=THT]
  J4 = female pin header, 3 pins [form="♀ (female)"]
  R3 = Resistor [tolerance=±5% power=0.25W resistance=1000 package=THT]

nets:
  N1: Adafruit_TMC2209_Stepper_Motor_Driver1.OUT1B, M2.D
  N2: Adafruit_TMC2209_Stepper_Motor_Driver1.OUT1A, M2.B
  N3: Adafruit_TMC2209_Stepper_Motor_Driver1.OUT2A, M2.C
  N4: Adafruit_TMC2209_Stepper_Motor_Driver1.OUT2B, M2.A
  N5: Adafruit_TMC2209_Stepper_Motor_Driver1.GND, 12V_5-10A_DC.NEG, 25V_100mf.-, J1.pin1, J1.pin2
  N6: Adafruit_TMC2209_Stepper_Motor_Driver1.VMOTOR, 12V_5-10A_DC.POS, M3.Pin_1, 25V_100mf.+
  VDD: Adafruit_TMC2209_Stepper_Motor_Driver1.VDD, esp1.3V3, J4.pin2
  N7: Adafruit_TMC2209_Stepper_Motor_Driver1.DIR, esp1.IO14
  N8: Adafruit_TMC2209_Stepper_Motor_Driver1.STEP, esp1.IO27
  N9: Adafruit_TMC2209_Stepper_Motor_Driver1.MS1, J1.pin3
  N10: Adafruit_TMC2209_Stepper_Motor_Driver1.MS2, J1.pin4
  N11: Adafruit_TMC2209_Stepper_Motor_Driver1.DIAG, esp1.IO25
  N12: Adafruit_TMC2209_Stepper_Motor_Driver1.UART, J2.pin3
  N13: Adafruit_TMC2209_Stepper_Motor_Driver1.ENABLE, esp1.IO13
  N14: esp1.IO22, R3.Pin_1
  N15: esp1.IO23, J2.pin2
  N16: esp1.GND, J1.pin10
  N17: esp1.IO34, R2.Pin_1
  N18: esp1.5V, M3.Pin_3
  N19: M3.Pin_2, M3.Pin_4, J1.pin9
  N20: R2.Pin_0, J4.pin3
  N21: J1.pin5, R1.pin_0
  N22: J2.pin1, R3.Pin_0
  N23: R1.pin_1, J4.pin1

custom parts:
  ESP32 DevKitc V4: ESP32-DevKitC board with ESP32-WROOM-32 module. ESP32-DevKitC V4 is a small-sized ESP32-based development board produced by Espressif. Most of the pins on the ESP module are broken out to the pin headers on the board. The pins D0, D1, D2, D3, CMD and CLK are used internally for communication between ESP32 and SPI flash memory. They are grouped on both sides near the USB connector. Avoid using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
